# Fritzing sketch eeprom-hat-led-pcb (saved by Fritzing 0.9.2b)
stripboards: 1
perfboards: 1

parts:
  R1 = Resistor [tolerance=±5% resistance=3.9k package="1206 [SMD]"]
  LED1 = RGB LED (com. anode, rbg) [package="5 mm [THT]"]
  U2 = IC, DIP package, 8 pins [chip_label=CAT24C32]
  R3 = Resistor [tolerance=±5% resistance=220 package="0603 [SMD]"]
  JP1 = Header 10 [package=1x10-2mm-smd]  # not connected
  JP2 = Header 10 [package=1x10-2mm-smd]  # not connected
  JP3 = Header 10 [package=1x10-2mm-smd]  # not connected
  JP4 = Header 10 [package=1x10-2mm-smd]  # not connected
  R6 = Resistor [tolerance=±5% resistance=3.9k package="1206 [SMD]"]
  R7 = Resistor [tolerance=±5% resistance=220 package="0603 [SMD]"]
  R8 = Resistor [tolerance=±5% resistance=220 package="0603 [SMD]"]

nets:
  N1: R1.Pin_0, U2.pin8, R6.Pin_0
  N2: R1.Pin_1, U2.pin5
  N3: LED1.red_cathode, R8.Pin_1
  N4: LED1.common_anode, R7.Pin_1
  N5: LED1.blue_cathode, U2.pin4
  N6: LED1.green_cathode, R3.Pin_1
  N7: U2.pin6, R6.Pin_1
